# Fritzing sketch input (saved by Fritzing 0.8.3b)
breadboards: 1

parts:
  R1 = Resistor [tolerance=±5% resistance=10k package=THT]
  Raspberry_Pi1 = Raspberry Pi (Model B)
  LED1 = LED - 5mm [color="Red (633nm)" package="5 mm [THT]"]
  R2 = Resistor [tolerance=±5% resistance=10k package=THT]
  S1 = Pushbutton [package="[THT]"]
  LED2 = LED - 5mm [color="Red (633nm)" package="5 mm [THT]"]
  R3 = Resistor [tolerance=±5% resistance=10k package=THT]

nets:
  N1: R1.Pin_0, Raspberry_Pi1.GND, R2.Pin_1, R3.Pin_0
  N2: R1.Pin_1, LED1.cathode
  N3: Raspberry_Pi1.5V, S1.Pin_3, S1.Pin_4
  N4: Raspberry_Pi1.#18, LED1.anode
  N5: Raspberry_Pi1.#21, R2.Pin_0, S1.Pin_1, S1.Pin_2
  N6: Raspberry_Pi1.#22, LED2.anode
  N7: LED2.cathode, R3.Pin_1

custom parts:
  Raspberry Pi (Model B): Raspberry Pi Single-board Computer, Model B
