# Fritzing sketch shellScript (saved by Fritzing 0.7.10b)
breadboards: 1

parts:
  R1 = Resistor [tolerance=±5% resistance=10k package=THT]
  Raspberry_Pi1 = Raspberry Pi (Model B)
  LED1 = LED - 5mm [color="Red (633nm)" package="5 mm [THT]"]

nets:
  N1: R1.Pin_0, Raspberry_Pi1.GND
  N2: R1.Pin_1, LED1.cathode
  N3: Raspberry_Pi1.#4, LED1.anode

custom parts:
  Raspberry Pi (Model B): Raspberry Pi Single-board Computer, Model B
