# Fritzing sketch raspberry_arduino_usb (saved by Fritzing 0.7.10b)
breadboards: 1

parts:
  Raspberry_Pi1 = Raspberry Pi (Model B)  # not connected
  Arduino1 = Arduino
  R1 = Resistor [tolerance=±5% resistance=1k package=THT]
  R2 = Photocell (LDR) [package=THT]
  LED1 = LED - 5mm [color="Red (633nm)" package="5 mm [THT]"]
  R3 = Resistor [tolerance=±5% resistance=1k package=THT]
  X1 = USB Connectors [package=usb-minib-nostop]  # not connected

nets:
  N1: Arduino1.GND, R1.Pin_1, R3.Pin_1
  N2: Arduino1.D13, LED1.anode
  N3: Arduino1.+5V, R2.pin_1
  N4: Arduino1.A0, R1.Pin_0, R2.pin_0
  N5: LED1.cathode, R3.Pin_0

custom parts:
  Raspberry Pi (Model B): Raspberry Pi Single-board Computer, Model B
