# Fritzing sketch 13-4-Radio (saved by Fritzing 0.7.10b)
breadboards: 1

parts:
  R1 = Resistor [tolerance=±5% resistance=10k package=THT]
  Raspberry_Pi1 = Raspberry Pi (Model B)
  S1 = Pushbutton [package="[THT]"]
  R3 = Resistor [tolerance=±5% resistance=10k package=THT]
  S2 = Pushbutton [package="[THT]"]

nets:
  N1: R1.Pin_0, Raspberry_Pi1.#24, S1.Pin_1, S1.Pin_2
  N2: R1.Pin_1, Raspberry_Pi1.GND, R3.Pin_1
  N3: Raspberry_Pi1.5V, S1.Pin_3, S1.Pin_4, S2.Pin_3, S2.Pin_4
  N4: Raspberry_Pi1.#23, R3.Pin_0, S2.Pin_1, S2.Pin_2

custom parts:
  Raspberry Pi (Model B): Raspberry Pi Single-board Computer, Model B
