# Fritzing sketch 15-6 (saved by Fritzing 0.7.10b)
breadboards: 1

parts:
  S1 = Pushbutton [package="[THT]"]
  R1 = Resistor [tolerance=±5% resistance=10k package=THT]
  Raspberry_Pi1 = Raspberry Pi (Model B)
  S2 = Pushbutton [package="[THT]"]
  R2 = Resistor [tolerance=±5% resistance=10k package=THT]

nets:
  N1: S1.Pin_1, S1.Pin_2, R1.Pin_0, Raspberry_Pi1.#23
  N2: S1.Pin_3, S1.Pin_4, Raspberry_Pi1.5V, S2.Pin_3, S2.Pin_4
  N3: R1.Pin_1, Raspberry_Pi1.GND, R2.Pin_1
  N4: Raspberry_Pi1.#24, S2.Pin_1, S2.Pin_2, R2.Pin_0

custom parts:
  Raspberry Pi (Model B): Raspberry Pi Single-board Computer, Model B
