# Fritzing sketch camera (saved by Fritzing 0.7.10b)
breadboards: 1

parts:
  S1 = Pushbutton [package="[THT]"]
  R1 = Resistor [tolerance=±5% resistance=10k package=THT]
  Raspberry_Pi1 = Raspberry Pi (Model B)

nets:
  N1: S1.Pin_1, S1.Pin_2, R1.Pin_0, Raspberry_Pi1.#23
  N2: S1.Pin_3, S1.Pin_4, Raspberry_Pi1.5V
  N3: R1.Pin_1, Raspberry_Pi1.GND

custom parts:
  Raspberry Pi (Model B): Raspberry Pi Single-board Computer, Model B
