# Fritzing sketch analog_outB (saved by Fritzing 0.7.10b)
breadboards: 1

parts:
  R1 = Resistor [tolerance=±5% resistance=10k package=THT]
  LED1 = LED - 5mm [color="Red (633nm)" package="5 mm [THT]"]
  Raspberry_Pi1 = Raspberry Pi (Model B)
  R2 = Resistor [tolerance=±5% resistance=3.9k package=THT]
  C1 = Ceramic Capacitor [capacitance=0.1µF voltage=10V package="100 mil [THT, multilayer]"]

nets:
  N1: R1.Pin_0, Raspberry_Pi1.GND, C1.0
  N2: R1.Pin_1, LED1.cathode
  N3: LED1.anode, R2.Pin_0, C1.1
  N4: Raspberry_Pi1.#4, R2.Pin_1

custom parts:
  Raspberry Pi (Model B): Raspberry Pi Single-board Computer, Model B
