# Fritzing sketch edge (saved by Fritzing 0.7.10b)
breadboards: 1

parts:
  R1 = Resistor [tolerance=±5% resistance=10k package=THT]
  Raspberry_Pi1 = Raspberry Pi (Model B)
  R2 = Resistor [tolerance=±5% resistance=10k package=THT]
  S1 = Pushbutton [package="[THT]"]
  S2 = Pushbutton [package="[THT]"]

nets:
  N1: R1.Pin_0, Raspberry_Pi1.#4, S2.Pin_1, S2.Pin_2
  N2: R1.Pin_1, Raspberry_Pi1.GND, R2.Pin_1
  N3: Raspberry_Pi1.5V, S1.Pin_3, S1.Pin_4, S2.Pin_3, S2.Pin_4
  N4: Raspberry_Pi1.#17, R2.Pin_0, S1.Pin_1, S1.Pin_2

custom parts:
  Raspberry Pi (Model B): Raspberry Pi Single-board Computer, Model B
